# Fritzing sketch scxh (saved by Fritzing 0.9.3b)
breadboards: 2

parts:
  U1 = NodeMCU V1.0
  LED1 = LED - 5mm [color="Yellow (595nm)" package="5 mm [THT]"]
  LED2 = LED - 5mm [color="Red (633nm)" package="5 mm [THT]"]  # not connected

nets:
  N1: U1.D1, LED1.anode
  N2: U1.GND, LED1.cathode

custom parts:
  NodeMCU V1.0: ESP8266 based NodeMCU
